// Logisim project BCD.circ as structural Verilog: 1 circuit, main circuit main
module main (
  input  A3,
  input  A2,
  input  A1,
  input  A0,
  input  B3,
  input  B2,
  input  B1,
  input  B0,
  input  in_9,
  output FC,
  output R3,
  output R2,
  output R1,
  output R0
);

  wire and_1_out, and_2_out, main_1_c, main_1_s0, main_1_s1, main_1_s2, main_1_s3, or_1_out;

  or or_1 (or_1_out, main_1_c, and_1_out, and_2_out);
  and and_1 (and_1_out, main_1_s3, main_1_s2);
  and and_2 (and_2_out, main_1_s3, main_1_s1);
  BPA_4bit__main main_1 (
    .B3(B3), .A3(A3), .B2(B2), .A2(A2), .B1(B1), .A1(A1), .B0(B0), .A0(A0), .C(main_1_c), .S3(main_1_s3),
    .S2(main_1_s2), .S1(main_1_s1), .S0(main_1_s0));
  BPA_4bit__main main_2 (
    .B3(in_9), .A3(main_1_s3), .B2(or_1_out), .A2(main_1_s2), .B1(or_1_out), .A1(main_1_s1), .B0(in_9),
    .A0(main_1_s0), .C(FC), .S3(R3), .S2(R2), .S1(R1), .S0(R0));

  // Notes on the sheet:
  //   BINARY CODED DECIMAL
  //   4 BPA
  //   4 BPA
endmodule
