// Logisim project BPA(4bit).circ as structural Verilog: 1 circuit, main circuit main
module main (
  input  A3,
  input  A2,
  input  A1,
  input  A0,
  input  B3,
  input  B2,
  input  B1,
  input  B0,
  output C,
  output S3,
  output S2,
  output S1,
  output S0
);

  wire main_1_p4, main_2_p4, main_3_p4;

  // FA_main main_1: pin names not known; wires that end beside it: B3, A3, C, main_1_p4, S3
  // FA_main main_2: pin names not known; wires that end beside it: B2, A2, main_1_p4, main_2_p4, S2
  // FA_main main_3: pin names not known; wires that end beside it: B1, A1, main_2_p4, main_3_p4, S1
  // HA_main main_4: pin names not known; wires that end beside it: B0, main_3_p4, A0, S0

  // Notes on the sheet:
  //   BINARY PARALLEL ADDER (4 BIT)
endmodule
