// Logisim project CLA.circ as structural Verilog: 1 circuit, main circuit main
module main (
  input  B2,
  input  A2,
  input  B1,
  input  A1,
  input  B0,
  input  A0,
  input  C_1,
  output C2,
  output C1,
  output C0
);

  wire and_2_out, and_3_out, and_4_out, and_5_out, and_6_out, and_7_out, and_8_out, and_9_out, xor_1_out,
       xor_2_out, xor_3_out;

  xor xor_1 (xor_1_out, A2, B2);
  // AND_Gate and_1 has open pins: in0=B2, in1=A2, out=open
  xor xor_2 (xor_2_out, A1, B1);
  and and_2 (and_2_out, B1, A1);
  xor xor_3 (xor_3_out, A0, B0);
  and and_3 (and_3_out, B0, A0);
  and and_4 (and_4_out, xor_1_out, and_2_out);
  and and_5 (and_5_out, xor_1_out, xor_2_out, and_3_out);
  and and_6 (and_6_out, xor_1_out, xor_2_out, and_3_out);
  and and_7 (and_7_out, xor_2_out, and_3_out);
  and and_8 (and_8_out, xor_2_out, and_3_out, C_1);
  and and_9 (and_9_out, xor_3_out, C_1);
  or or_1 (C0, and_9_out, and_3_out);
  or or_2 (C2, and_4_out, and_5_out, and_6_out);
  or or_3 (C1, and_7_out, and_8_out, and_2_out);

  // Notes on the sheet:
  //   CARRY LOOK AHEAD ADDER
endmodule
