// Logisim project D FF(CLK).circ as structural Verilog: 1 circuit, main circuit main
module main (
  input  D,
  output Q_prime,
  output Q
);

  wire and_1_out, and_2_out, clk_out, not_1_out;

  not not_1 (not_1_out, D);
  Clock clk (.out(clk_out));
  and and_1 (and_1_out, D, clk_out);
  and and_2 (and_2_out, clk_out, not_1_out);
  nor nor_1 (Q_prime, and_1_out, Q);
  nor nor_2 (Q, Q_prime, and_2_out);

  // Notes on the sheet:
  //   D FLIP FLOP (CLOCK)
endmodule
