// Logisim project D FLIP FLOP(NOR).circ as structural Verilog: 1 circuit, main circuit main
module main (
  input  D,
  output Q_prime,
  output Q
);

  wire not_1_out;

  not not_1 (not_1_out, D);
  nor nor_1 (Q_prime, D, Q);
  nor nor_2 (Q, Q_prime, not_1_out);

  // Notes on the sheet:
  //   D FLIP FLOP (USING NOR)
endmodule
