// Logisim project DECODER(2X4).circ as structural Verilog: 1 circuit, main circuit main
module main (
  input  X,
  input  Y,
  output D0,
  output D1,
  output D2,
  output D3
);

  wire not_1_out, not_2_out;

  not not_1 (not_1_out, X);
  not not_2 (not_2_out, Y);
  and and_1 (D0, not_1_out, not_2_out);
  and and_2 (D1, not_1_out, Y);
  and and_3 (D2, X, not_2_out);
  and and_4 (D3, X, Y);

  // Notes on the sheet:
  //   DECODER (2X4)
endmodule
