// Logisim project DECODER(3X8).circ as structural Verilog: 1 circuit, main circuit main
module main (
  input  X,
  input  Y,
  input  Z,
  output D0,
  output D1,
  output D2,
  output D3,
  output D4,
  output D5,
  output D6,
  output D7
);

  wire not_1_out, not_2_out, not_3_out;

  not not_1 (not_1_out, X);
  not not_2 (not_2_out, Y);
  not not_3 (not_3_out, Z);
  and and_1 (D0, not_1_out, not_2_out, not_3_out);
  and and_2 (D1, not_1_out, not_2_out, Z);
  and and_3 (D2, not_1_out, Y, not_3_out);
  and and_4 (D3, not_1_out, Y, Z);
  and and_5 (D4, X, not_2_out, not_3_out);
  and and_6 (D5, X, not_2_out, Z);
  and and_7 (D6, X, Y, not_3_out);
  and and_8 (D7, X, Y, Z);

  // Notes on the sheet:
  //   DECODER(3X8)
endmodule
