// Logisim project ENCODER (8X3).circ as structural Verilog: 1 circuit, main circuit main
module main (
  input  D7,
  input  D6,
  input  D5,
  input  D4,
  input  D3,
  input  D2,
  input  D1,
  input  D0,
  output A,
  output B,
  output C
);

  or or_1 (A, D7, D6, D4, D5);
  or or_2 (B, D7, D6, D3, D2);
  or or_3 (C, D7, D5, D3, D1);

  // Notes on the sheet:
  //   ENCODER (8X3)
endmodule
