// Logisim project ENCODER(4X2).circ as structural Verilog: 1 circuit, main circuit main
module main (
  input  D3,
  input  D2,
  input  D1,
  input  D0,
  output A,
  output B
);

  or or_1 (A, D3, D2);
  or or_2 (B, D1, D3);

  // Notes on the sheet:
  //   ENCODER (4X2)
endmodule
