// Logisim project Full Adder.circ as structural Verilog: 1 circuit, main circuit main
module main (
  input  X,
  input  Y,
  input  Z,
  output S,
  output C
);

  wire and_1_out, and_2_out, xor_1_out;

  xor xor_1 (xor_1_out, X, Y);
  and and_1 (and_1_out, xor_1_out, Z);
  and and_2 (and_2_out, X, Y);
  xor xor_2 (S, xor_1_out, Z);
  or or_1 (C, and_1_out, and_2_out);

  // Notes on the sheet:
  //   FULL ADDER
endmodule
