// Logisim project Full Subtractor.circ as structural Verilog: 1 circuit, main circuit main
module main (
  input  X,
  input  Y,
  input  Z,
  output D,
  output B
);

  wire and_1_out, and_2_out, not_1_out, not_2_out, xor_1_out;

  xor xor_1 (xor_1_out, X, Y);
  not not_1 (not_1_out, X);
  and and_1 (and_1_out, not_1_out, Y);
  xor xor_2 (D, xor_1_out, Z);
  not not_2 (not_2_out, xor_1_out);
  and and_2 (and_2_out, not_2_out, Z);
  or or_1 (B, and_2_out, and_1_out);

  // Notes on the sheet:
  //   FULL SUBTRACTOR
endmodule
