// Logisim project Half Subtractor.circ as structural Verilog: 1 circuit, main circuit main
module main (
  input  X,
  input  Y,
  output D,
  output B
);

  wire not_1_out;

  xor xor_1 (D, X, Y);
  not not_1 (not_1_out, X);
  and and_1 (B, not_1_out, Y);

  // Notes on the sheet:
  //   HALF SUBTRACTOR
endmodule
