// Logisim project MASTER SLAVE JK FF.circ as structural Verilog: 1 circuit, main circuit main
module main (
  input  J,
  input  CLK,
  input  K,
  output Q,
  output Q_prime
);

  wire main_1_p4, main_1_p5, not_1_out;

  // JK_FF__CLOCK__main main_1: pin names not known; wires that end beside it: J, CLK, K, main_1_p4, main_1_p5
  not not_1 (not_1_out, CLK);
  // JK_FF__CLOCK__main main_2: pin names not known; wires that end beside it: main_1_p4, not_1_out, main_1_p5, Q, Q_prime

  // Notes on the sheet:
  //   JK FLIP FLOP (CLOCK)
endmodule
