// Logisim project MULTIPLEXER (8X1).circ as structural Verilog: 1 circuit, main circuit main
module main (
  input  A,
  input  B,
  input  C,
  input  I7,
  input  I6,
  input  I5,
  input  I4,
  input  I3,
  input  I2,
  input  I1,
  input  I0,
  output Y
);

  wire and_1_out, and_2_out, and_3_out, and_4_out, and_5_out, and_6_out, and_7_out, and_8_out, not_1_out,
       not_2_out, not_3_out;

  not not_1 (not_1_out, A);
  not not_2 (not_2_out, B);
  not not_3 (not_3_out, C);
  and and_1 (and_1_out, I7, A, B, C);
  and and_2 (and_2_out, I6, A, B, not_3_out);
  and and_3 (and_3_out, I5, A, not_2_out, C);
  and and_4 (and_4_out, I4, A, not_2_out, not_3_out);
  and and_5 (and_5_out, I3, not_1_out, B, C);
  and and_6 (and_6_out, I2, not_1_out, B, not_3_out);
  and and_7 (and_7_out, I1, not_1_out, not_2_out, C);
  and and_8 (and_8_out, I0, not_1_out, not_2_out, not_3_out);
  or or_1 (Y, and_1_out, and_2_out, and_3_out, and_4_out, and_5_out, and_6_out, and_7_out, and_8_out);

  // Notes on the sheet:
  //   MULTIPLEXER (8X1)
endmodule
