// Logisim project MULTIPLEXER(4X1).circ as structural Verilog: 1 circuit, main circuit main
module main (
  input  A,
  input  B,
  input  I3,
  input  I2,
  input  I1,
  input  I0,
  output Y
);

  wire and_1_out, and_2_out, and_3_out, and_4_out, not_1_out, not_2_out;

  not not_1 (not_1_out, A);
  not not_2 (not_2_out, B);
  and and_1 (and_1_out, I3, A, B);
  and and_2 (and_2_out, I2, A, not_2_out);
  and and_3 (and_3_out, I1, not_1_out, B);
  and and_4 (and_4_out, I0, not_1_out, not_2_out);
  or or_1 (Y, and_1_out, and_2_out, and_3_out, and_4_out);

  // Notes on the sheet:
  //   MULTIPLEXER (4X1)
endmodule
