// Logisim project MULTIPLIER(2bit).circ as structural Verilog: 1 circuit, main circuit main
module main (
  input  A1,
  input  A0,
  input  B1,
  input  B0,
  output R0,
  output R1,
  output R2,
  output R3
);

  wire and_2_out, and_3_out, and_4_out, main_1_p4;

  and and_1 (R0, A0, B0);
  and and_2 (and_2_out, A1, B0);
  and and_3 (and_3_out, A0, B1);
  and and_4 (and_4_out, A1, A0);
  // HA_main main_1: pin names not known; wires that end beside it: and_2_out, and_3_out, R1, main_1_p4
  // HA_main main_2: pin names not known; wires that end beside it: main_1_p4, and_4_out, R2, R3

  // Notes on the sheet:
  //   BINARY MULTIPLIER (2 BIT)
  //   HA
  //   HA
endmodule
