// Logisim project MULTIPLIER(3bit).circ as structural Verilog: 1 circuit, main circuit main
module main (
  input  B0,
  input  A2,
  input  A1,
  input  A0,
  input  B1,
  input  A2_2,
  input  A1_2,
  input  A0_2,
  input  in_9,
  input  B2,
  input  A2_3,
  input  A1_3,
  input  A0_3,
  output R5,
  output R4,
  output R3,
  output R2,
  output R1,
  output R0
);

  wire and_1_out, and_2_out, and_3_out, and_4_out, and_5_out, and_6_out, and_7_out, and_8_out, main_1_c,
       main_1_s1, main_1_s2;

  and and_1 (and_1_out, B1, A2_2);
  and and_2 (and_2_out, B2, A2_3);
  and and_3 (and_3_out, B1, A1_2);
  and and_4 (and_4_out, B2, A1_3);
  and and_5 (and_5_out, B1, A0_2);
  and and_6 (and_6_out, B2, A0_3);
  and and_7 (and_7_out, B0, A2);
  BPA_3bit__main main_1 (
    .B2(and_1_out), .A2(in_9), .B1(and_3_out), .A1(and_7_out), .B0(and_5_out), .A0(and_8_out), .C(main_1_c),
    .S2(main_1_s2), .S1(main_1_s1), .S0(R1));
  BPA_3bit__main main_2 (
    .B2(and_2_out), .A2(main_1_c), .B1(and_4_out), .A1(main_1_s2), .B0(and_6_out), .A0(main_1_s1), .C(R5),
    .S2(R4), .S1(R3), .S0(R2));
  and and_8 (and_8_out, B0, A1);
  and and_9 (R0, B0, A0);

  // Notes on the sheet:
  //   BINARY MULTIPLIER (3 BIT)
  //   3 BPA
  //   3 BPA
endmodule
