// Logisim project MULTIPLIER(4bit).circ as structural Verilog: 1 circuit, main circuit main
module main (
  input  B0,
  input  A3,
  input  A2,
  input  A1,
  input  A0,
  input  B1,
  input  in_7,
  input  A3_2,
  input  A2_2,
  input  A1_2,
  input  A0_2,
  input  B2,
  input  A3_3,
  input  A2_3,
  input  A1_3,
  input  A0_3,
  input  B3,
  input  A3_4,
  input  A2_4,
  input  A1_4,
  input  A0_4,
  output R7,
  output R6,
  output R5,
  output R4,
  output R3,
  output R2,
  output R1,
  output R0
);

  wire and_1_out, and_2_out, and_3_out, and_4_out, and_5_out, and_6_out, and_7_out, and_8_out, and_9_out,
       and_10_out, and_11_out, and_12_out, and_13_out, and_14_out, and_15_out, main_1_c, main_1_s1,
       main_1_s2, main_1_s3, main_3_c, main_3_s1, main_3_s2, main_3_s3;

  and and_1 (and_1_out, B1, A3_2);
  and and_2 (and_2_out, B1, A2_2);
  and and_3 (and_3_out, B2, A3_3);
  and and_4 (and_4_out, B2, A2_3);
  and and_5 (and_5_out, B3, A2_4);
  and and_6 (and_6_out, B3, A3_4);
  and and_7 (and_7_out, B1, A1_2);
  and and_8 (and_8_out, B2, A1_3);
  and and_9 (and_9_out, B3, A1_4);
  and and_10 (and_10_out, B3, A0_4);
  and and_11 (and_11_out, B0, A3);
  and and_12 (and_12_out, B1, A0_2);
  and and_13 (and_13_out, B2, A0_3);
  BPA_4bit__main main_1 (
    .B3(and_3_out), .A3(main_3_c), .B2(and_4_out), .A2(main_3_s3), .B1(and_8_out), .A1(main_3_s2),
    .B0(and_13_out), .A0(main_3_s1), .C(main_1_c), .S3(main_1_s3), .S2(main_1_s2), .S1(main_1_s1), .S0(R2));
  BPA_4bit__main main_2 (
    .B3(and_6_out), .A3(main_1_c), .B2(and_5_out), .A2(main_1_s3), .B1(and_9_out), .A1(main_1_s2),
    .B0(and_10_out), .A0(main_1_s1), .C(R7), .S3(R6), .S2(R5), .S1(R4), .S0(R3));
  and and_14 (and_14_out, B0, A2);
  and and_15 (and_15_out, B0, A1);
  BPA_4bit__main main_3 (
    .B3(and_1_out), .A3(in_7), .B2(and_2_out), .A2(and_11_out), .B1(and_7_out), .A1(and_14_out),
    .B0(and_12_out), .A0(and_15_out), .C(main_3_c), .S3(main_3_s3), .S2(main_3_s2), .S1(main_3_s1), .S0(R1));
  and and_16 (R0, B0, A0);

  // Notes on the sheet:
  //   4 BPA
  //   BINARY MULTIPLIER (4 BIT)
  //   4 BPA
endmodule
