// Logisim project PRIORITY ENCODER.circ as structural Verilog: 1 circuit, main circuit main
module main (
  input  D3,
  input  D2,
  input  D1,
  input  D0,
  output A,
  output B,
  output V
);

  wire and_1_out, and_2_out, and_3_out, not_1_out;

  not not_1 (not_1_out, D2);
  and and_1 (and_1_out, not_1_out, D1);
  and and_2 (and_2_out, D1, not_1_out);
  and and_3 (and_3_out, not_1_out, D0);
  or or_1 (A, D3, D2);
  or or_2 (B, and_1_out, D3);
  or or_3 (V, D2, D3, and_2_out, and_3_out);

  // Notes on the sheet:
  //   PRIORITY ENCODER
endmodule
