// Logisim project Q MULTIPLEXER.circ as structural Verilog: 1 circuit, main circuit main
module main (
  input  I,
  input  A,
  input  B,
  output D3,
  output D2,
  output D1,
  output D0
);

  wire not_1_out, not_2_out;

  not not_1 (not_1_out, A);
  not not_2 (not_2_out, B);
  and and_1 (D3, I, A, B);
  and and_2 (D2, I, A, not_2_out);
  and and_3 (D1, I, not_1_out, B);
  and and_4 (D0, I, not_1_out, not_2_out);

  // Notes on the sheet:
  //   Q MULTIPLEXER
endmodule
