// Logisim project SR FF (CLOCK).circ as structural Verilog: 1 circuit, main circuit main
module main (
  input  S,
  input  R,
  output out_3,
  output out_4
);

  wire and_1_out, and_2_out, clock_1_out;

  Clock clock_1 (.out(clock_1_out));
  and and_1 (and_1_out, S, clock_1_out);
  and and_2 (and_2_out, clock_1_out, R);
  nor nor_1 (out_3, and_1_out, out_4);
  nor nor_2 (out_4, out_3, and_2_out);

  // Notes on the sheet:
  //   SR FLIP FLOP (CLOCK)
endmodule
