// Logisim project SR FF (NOR).circ as structural Verilog: 1 circuit, main circuit main
module main (
  input  S,
  input  R,
  output Q_prime,
  output Q
);

  nor nor_1 (Q_prime, S, Q);
  nor nor_2 (Q, Q_prime, R);

  // Notes on the sheet:
  //   SR FLIP FLOP (USING NOR)
endmodule
