// Logisim project SR FF(NAND).circ as structural Verilog: 1 circuit, main circuit main
module main (
  input  S,
  input  R,
  output Q_prime,
  output Q
);

  wire and_1_out, nand_1_out;

  and and_1 (and_1_out, S, S);
  nand nand_1 (nand_1_out, R, R);
  nand nand_2 (Q_prime, and_1_out, Q);
  nand nand_3 (Q, Q_prime, nand_1_out);

  // Notes on the sheet:
  //   SR FLIP FLOP (USING NAND)
endmodule
