// Logisim project T FF (CLK).circ as structural Verilog: 1 circuit, main circuit main
module main (
  input  T,
  output Q_prime,
  output Q
);

  wire and_1_out, and_2_out, clk_out;

  Clock clk (.out(clk_out));
  and and_1 (and_1_out, Q_prime, T, clk_out);
  and and_2 (and_2_out, clk_out, T, Q);
  nor nor_1 (Q_prime, and_1_out, Q);
  nor nor_2 (Q, Q_prime, and_2_out);

  // Notes on the sheet:
  //   T FLIP FLOP (CLOCK)
endmodule
