// Logisim project TFF (NAND).circ as structural Verilog: 1 circuit, main circuit main
module main (
  input  T,
  output Q,
  output Q_prime
);

  wire nand_1_out, nand_2_out;

  nand nand_1 (nand_1_out, Q_prime, T);
  nand nand_2 (nand_2_out, T, Q);
  nand nand_3 (Q, nand_1_out, Q_prime);
  nand nand_4 (Q_prime, Q, nand_2_out);

  // Notes on the sheet:
  //   T FLIP FLOP (USING NAND)
endmodule
