// Logisim project coounter.circ as structural Verilog: 1 circuit, main circuit main
module main (
  output out_1,
  output out_2,
  output out_3,
  output out_4,
  output out_5,
  output out_6
);

  wire and_1_out, clock_1_out, undriven, undriven_2, undriven_3, undriven_4, undriven_5, undriven_6,
       undriven_7, undriven_8, undriven_9;

  Clock clock_1 (.out(clock_1_out));
  J_K_Flip_Flop j_k_ff_1 (
    .J(and_1_out), .clk(clock_1_out), .K(and_1_out), .Q(out_1), .Qn(out_4), .preset(undriven),
    .en(undriven_2), .reset(undriven_3));
  and and_1 (and_1_out, out_3, out_2);
  J_K_Flip_Flop j_k_ff_2 (
    .J(out_3), .clk(clock_1_out), .K(out_3), .Q(out_2), .Qn(out_5), .preset(undriven_4), .en(undriven_5),
    .reset(undriven_6));
  J_K_Flip_Flop j_k_ff_3 (
    .J(out_3), .clk(clock_1_out), .K(out_3), .Q(out_3), .Qn(out_6), .preset(undriven_7), .en(undriven_8),
    .reset(undriven_9));
endmodule
